# Fritzing sketch circuit (saved by Fritzing 0.9.3b)
breadboards: 1

parts:
  Part1 = Arduino MKR1000  # not connected
  LED1 = RGB LED (com. cathode, rgb) [package="5 mm [THT]"]  # not connected
  LCD1 = LCD screen
  RE1 = Rotary Encoder [package=THT]  # not connected
  T1 = LM35 Temperature Sensor [package="TO92 [THT]"]  # not connected
  R1 = Resistor [tolerance=±5% resistance=220 package=THT]

nets:
  N1: LCD1.LED+, R1.Pin_1

custom parts:
  Arduino MKR1000: MKR1000 is a powerful board that combines the functionality of the Zero and the Wi-Fi Shield. It is the ideal solution for makers wanting to design IoT projects with minimal previous experience in networking
